# Fritzing sketch FF5O2C5HUCTRJK7 (saved by Fritzing 0.8.7b)
breadboards: 1

parts:
  Part1 = Arduino Uno (Rev3)
  DI1 = 7-Segment LED Display [package=THT]
  R1 = Resistor [tolerance=±5% resistance=220 package=THT]
  R2 = Resistor [tolerance=±5% resistance=220 package=THT]

nets:
  N1: Part1.D8, DI1.cathodeF
  N2: Part1.D9_PWM, DI1.cathodeG
  N3: Part1.D2, DI1.cathodeA
  N4: Part1.D3_PWM, DI1.cathodeB
  N5: Part1.D4, DI1.cathodeC
  N6: Part1.D5_PWM, DI1.cathodeD
  N7: Part1.D6_PWM, DI1.cathodeE
  N8: Part1.GND, R1.Pin_1, R2.Pin_1
  N9: DI1.commAnode#2, R2.Pin_0
  N10: DI1.commAnode#7, R1.Pin_0
